// Logisim project ALU_SevenSegment.circ as structural Verilog: 6 circuits, main circuit Final
module main (
  input  [4:0] A,
  input  [2:0] Selector,
  input  [4:0] B,
  output [4:0] Result
);

  wire [4:0] adder_1_out, and_1_out, divider_1_out, multiplier_1_out, or_1_out, subtractor_1_out;

  Adder #(.width(5)) adder_1 (.a(A), .b(B), .out(adder_1_out));  // open: cin, cout
  Subtractor #(.width(5)) subtractor_1 (.a(A), .b(B), .out(subtractor_1_out));  // open: bin, bout
  Multiplier #(.width(5)) multiplier_1 (.a(A), .b(B), .out(multiplier_1_out));  // open: cin, cout
  Divider #(.width(5)) divider_1 (.a(A), .b(B), .out(divider_1_out));  // open: upper, rem
  assign and_1_out = A & B;  // AND_Gate and_1, 5 bits wide
  assign or_1_out = A | B;  // OR_Gate or_1, 5 bits wide
  Multiplexer #(.select(3), .width(5), .enable("false")) multiplexer_1 (
    .in0({5{1'b0}}), .in1(adder_1_out), .in2(subtractor_1_out), .in3(multiplier_1_out), .in4(divider_1_out),
    .in5(and_1_out), .in6(or_1_out), .in7({5{1'b1}}), .out(Result), .sel(Selector));
endmodule

module Final (
  input  [4:0] in_1,
  input  [4:0] in_2,
  input  [2:0] in_3,
  output I,
  output out_5,
  output out_6,
  output out_7,
  output out_8,
  output DA,
  output DB,
  output DC,
  output DD,
  output DE,
  output DF,
  output DG
);

  wire and_1_out, and_2_out, and_3_out, and_4_out, and_5_out, and_6_out, and_7_out, and_8_out, and_9_out,
       and_10_out, and_11_out, and_12_out, and_13_out, and_14_out, and_15_out, and_16_out, and_17_out,
       and_18_out, and_19_out, and_20_out, and_21_out, and_22_out, and_23_out, and_24_out, and_25_out,
       and_26_out, and_27_out, and_28_out, and_29_out, and_30_out, and_31_out, and_32_out, and_33_out,
       not_1_out, not_2_out, not_3_out, not_4_out;
  wire [3:1] init_1_out_2;
  wire [4:0] main_1_result;

  and and_1 (and_1_out, init_1_out_2[2], not_1_out);
  main main_1 (.A(in_1), .Selector(in_3), .B(in_2), .Result(main_1_result));
  and and_2 (and_2_out, init_1_out_2[2], init_1_out_2[1]);
  or G (out_8, and_1_out, and_2_out);
  init init_1 (.in_1(main_1_result), .out_2({init_1_out_2, I}));
  and and_3 (and_3_out, init_1_out_2[3], init_1_out_2[2], not_3_out);
  and and_4 (and_4_out, ~out_5, out_6);  // AND_Gate
  and and_5 (and_5_out, ~out_5, out_8, I);  // AND_Gate
  and and_6 (and_6_out, ~out_8, ~out_6, ~I);  // AND_Gate
  and and_7 (and_7_out, out_5, ~out_8, ~out_6);  // AND_Gate
  and and_8 (and_8_out, ~out_5, ~out_6, ~I);  // AND_Gate
  and and_9 (and_9_out, ~out_8, ~out_6, ~I);  // AND_Gate
  and and_10 (and_10_out, ~out_5, out_6, I);  // AND_Gate
  and and_11 (and_11_out, ~out_5, ~out_8, out_6);  // AND_Gate
  and and_12 (and_12_out, out_5, ~out_8, ~out_6);  // AND_Gate
  and and_13 (and_13_out, ~out_5, out_8);  // AND_Gate
  and and_14 (and_14_out, ~out_5, ~out_6, ~I);  // AND_Gate
  and and_15 (and_15_out, ~out_5, out_6, I);  // AND_Gate
  and and_16 (and_16_out, out_5, ~out_8, ~out_6);  // AND_Gate
  and and_17 (and_17_out, ~out_5, out_8, ~out_6, I);  // AND_Gate
  and and_18 (and_18_out, ~out_8, ~out_6, ~I);  // AND_Gate
  and and_19 (and_19_out, ~out_5, ~out_8, out_6);  // AND_Gate
  and and_20 (and_20_out, ~out_5, out_6, ~I);  // AND_Gate
  and and_21 (and_21_out, ~out_8, ~out_6, ~I);  // AND_Gate
  and and_22 (and_22_out, ~out_5, ~out_8, ~out_6);  // AND_Gate
  and and_23 (and_23_out, ~out_5, out_6, ~I);  // AND_Gate
  and and_24 (and_24_out, ~out_5, ~out_6);  // AND_Gate
  and and_25 (and_25_out, out_5, ~out_8, ~out_6);  // AND_Gate
  and and_26 (and_26_out, ~out_5, out_8, ~I, out_6);  // AND_Gate
  and and_27 (and_27_out, out_5, ~out_8, ~out_6);  // AND_Gate
  and and_28 (and_28_out, ~out_5, out_8, ~out_6);  // AND_Gate
  and and_29 (and_29_out, ~out_5, ~out_8, out_6);  // AND_Gate
  and and_30 (and_30_out, ~out_5, out_6, ~I);  // AND_Gate
  not not_1 (not_1_out, init_1_out_2[3]);
  not not_2 (not_2_out, init_1_out_2[2]);
  and and_31 (and_31_out, not_1_out, init_1_out_2[1]);
  or H (out_6, and_3_out, and_31_out);
  not not_3 (not_3_out, init_1_out_2[1]);
  or or_1 (DA, and_4_out, and_5_out, and_6_out, and_7_out);
  or or_2 (DB, and_8_out, and_9_out, and_10_out, and_11_out, and_12_out);
  or or_3 (DC, and_13_out, and_14_out, and_15_out, and_16_out);
  or or_4 (DD, and_17_out, and_18_out, and_19_out, and_20_out);
  or or_5 (DE, and_21_out, and_22_out, and_23_out);
  or or_6 (DF, and_24_out, and_25_out, and_26_out);
  or or_7 (DG, and_27_out, and_28_out, and_29_out, and_30_out);
  and F (out_5, init_1_out_2[3], not_2_out, not_3_out);
  and and_32 (and_32_out, init_1_out_2[3], init_1_out_2[1]);
  or E (out_7, and_32_out, and_33_out);
  and and_33 (and_33_out, init_1_out_2[3], init_1_out_2[2]);
  not not_4 (not_4_out, out_7);
  _7_Segment_Display u_7_segment_display_1 (
    .f(1'b1), .a(not_4_out), .b(not_4_out), .e(1'b1), .d(not_4_out), .c(not_4_out));  // open: g, dp
  _7_Segment_Display u_7_segment_display_2 (.g(main_1_result[4]));  // open: f, a, b, e, d, c, dp
  _7_Segment_Display u_7_segment_display_3 (.g(DG), .f(DF), .a(DA), .b(DB), .e(DE), .d(DD), .c(DC));  // open: dp

  // Notes on the sheet:
  //   -Ve num
  //   ALU & Seven Segment
  //   Mahmoud Fathy 
  //   Marwa Abdel-Ghany
endmodule

module segment (
  input  [3:0] ABCD,
  output [6:0] out_2
);

  wire and_1_out, and_2_out, and_3_out, and_4_out, and_5_out, and_6_out, and_7_out, and_8_out, and_9_out,
       and_10_out, and_11_out, and_12_out, and_13_out, and_14_out, and_15_out, and_16_out, and_17_out,
       and_18_out, and_19_out, and_20_out, and_21_out, and_22_out, and_23_out, and_24_out, and_25_out,
       and_26_out, and_27_out;

  and and_1 (and_1_out, ~ABCD[3], ABCD[1]);  // AND_Gate
  and and_2 (and_2_out, ~ABCD[3], ABCD[2], ABCD[0]);  // AND_Gate
  and and_3 (and_3_out, ~ABCD[2], ~ABCD[1], ~ABCD[0]);  // AND_Gate
  and and_4 (and_4_out, ABCD[3], ~ABCD[2], ~ABCD[1]);  // AND_Gate
  and and_5 (and_5_out, ~ABCD[3], ~ABCD[1], ~ABCD[0]);  // AND_Gate
  and and_6 (and_6_out, ~ABCD[2], ~ABCD[1], ~ABCD[0]);  // AND_Gate
  and and_7 (and_7_out, ~ABCD[3], ABCD[1], ABCD[0]);  // AND_Gate
  and and_8 (and_8_out, ~ABCD[3], ~ABCD[2], ABCD[1]);  // AND_Gate
  and and_9 (and_9_out, ABCD[3], ~ABCD[2], ~ABCD[1]);  // AND_Gate
  and and_10 (and_10_out, ~ABCD[3], ABCD[2]);  // AND_Gate
  and and_11 (and_11_out, ~ABCD[3], ~ABCD[1], ~ABCD[0]);  // AND_Gate
  and and_12 (and_12_out, ~ABCD[3], ABCD[1], ABCD[0]);  // AND_Gate
  and and_13 (and_13_out, ABCD[3], ~ABCD[2], ~ABCD[1]);  // AND_Gate
  and and_14 (and_14_out, ~ABCD[3], ABCD[2], ~ABCD[1], ABCD[0]);  // AND_Gate
  and and_15 (and_15_out, ~ABCD[2], ~ABCD[1], ~ABCD[0]);  // AND_Gate
  and and_16 (and_16_out, ~ABCD[3], ~ABCD[2], ABCD[1]);  // AND_Gate
  and and_17 (and_17_out, ~ABCD[3], ABCD[1], ~ABCD[0]);  // AND_Gate
  and and_18 (and_18_out, ~ABCD[2], ~ABCD[1], ~ABCD[0]);  // AND_Gate
  and and_19 (and_19_out, ~ABCD[3], ~ABCD[2], ~ABCD[1]);  // AND_Gate
  and and_20 (and_20_out, ~ABCD[3], ABCD[1], ~ABCD[0]);  // AND_Gate
  and and_21 (and_21_out, ~ABCD[3], ~ABCD[1]);  // AND_Gate
  and and_22 (and_22_out, ABCD[3], ~ABCD[2], ~ABCD[1]);  // AND_Gate
  and and_23 (and_23_out, ~ABCD[3], ABCD[2], ~ABCD[0], ABCD[1]);  // AND_Gate
  and and_24 (and_24_out, ABCD[3], ~ABCD[2], ~ABCD[1]);  // AND_Gate
  and and_25 (and_25_out, ~ABCD[3], ABCD[2], ~ABCD[1]);  // AND_Gate
  and and_26 (and_26_out, ~ABCD[3], ~ABCD[2], ABCD[1]);  // AND_Gate
  and and_27 (and_27_out, ~ABCD[3], ABCD[1], ~ABCD[0]);  // AND_Gate
  or or_1 (out_2[0], and_1_out, and_2_out, and_3_out, and_4_out);
  or or_2 (out_2[2], and_10_out, and_11_out, and_12_out, and_13_out);
  or or_3 (out_2[1], and_5_out, and_6_out, and_7_out, and_8_out, and_9_out);
  or or_4 (out_2[3], and_14_out, and_15_out, and_16_out, and_17_out);
  or or_5 (out_2[4], and_18_out, and_19_out, and_20_out);
  or or_6 (out_2[5], and_21_out, and_22_out, and_23_out);
  or or_7 (out_2[6], and_24_out, and_25_out, and_26_out, and_27_out);
endmodule

module BCD (
  input  [4:0] in_1,
  output [4:0] out_2
);

  wire and_1_out, and_2_out, and_3_out, and_4_out, and_5_out, and_6_out, not_1_out, not_2_out, not_3_out;

  and and_1 (and_1_out, in_1[2], not_1_out);
  or G (out_2[2], and_1_out, and_2_out);
  and and_2 (and_2_out, in_1[2], in_1[1]);
  and and_3 (and_3_out, in_1[3], in_1[2], not_3_out);
  not not_1 (not_1_out, in_1[3]);
  or H (out_2[1], and_3_out, and_4_out);
  not not_2 (not_2_out, in_1[2]);
  and and_4 (and_4_out, not_1_out, in_1[1]);
  not not_3 (not_3_out, in_1[1]);
  and F (out_2[3], in_1[3], not_2_out, not_3_out);
  and and_5 (and_5_out, in_1[3], in_1[1]);
  and and_6 (and_6_out, in_1[3], in_1[2]);
  or E (out_2[4], and_5_out, and_6_out);

  assign out_2[0] = in_1[0];
endmodule

module init (
  input  [4:0] in_1,
  output [3:0] out_2
);

  wire [3:0] bit_extender_1_out, xor_1_out;

  xor xor_1 (xor_1_out[0], in_1[4], in_1[0]);
  xor xor_2 (xor_1_out[1], in_1[4], in_1[1]);
  xor xor_3 (xor_1_out[2], in_1[4], in_1[2]);
  xor xor_4 (xor_1_out[3], in_1[4], in_1[3]);
  assign bit_extender_1_out = {{3{1'b0}}, in_1[4]};  // Bit_Extender bit_extender_1
  Adder #(.width(4)) adder_1 (.a(xor_1_out), .b(bit_extender_1_out), .out(out_2));  // open: cin, cout
endmodule

module the_final_2 (
  input  [4:0] in_1,
  input  [4:0] in_2,
  input  [2:0] in_3,
  output [4:0] out_4,
  output [4:0] out_5
);

  wire and_1_out, and_2_out, not_1_out;
  wire [3:0] init_1_out_2;
  wire [6:0] segment_1_out_2;

  main main_1 (.A(in_1), .Selector(in_3), .B(in_2), .Result(out_5));
  init init_1 (.in_1(out_5), .out_2(init_1_out_2));
  and and_1 (and_1_out, out_5[4], out_4[4]);
  _7_Segment_Display u_7_segment_display_1 (.g(and_1_out));  // open: f, a, b, e, d, c, dp
  and and_2 (and_2_out, out_5[4], not_1_out);
  _7_Segment_Display u_7_segment_display_2 (.g(and_2_out), .f(out_4[4]), .e(out_4[4]));  // open: a, b, d, c, dp
  BCD bcd_1 (.in_1({out_5[4], init_1_out_2}), .out_2(out_4));
  not not_1 (not_1_out, out_4[4]);
  _7_Segment_Display u_7_segment_display_3 (
    .g(segment_1_out_2[6]), .f(segment_1_out_2[5]), .a(segment_1_out_2[0]), .b(segment_1_out_2[1]),
    .e(segment_1_out_2[4]), .d(segment_1_out_2[3]), .c(segment_1_out_2[2]));  // open: dp
  segment segment_1 (.ABCD(out_4[3:0]), .out_2(segment_1_out_2));

  // Notes on the sheet:
  //   Marwa El-Oufy
  //   Mahmoud Fathy
  //   Section: 3
  //   Selection Bits
  //   ALU with Seven Segment Display
  //   l
  //   ____________________
  //   l
  //   GND
  //   000
  //   l
  //   l
  //   Addition
  //   001
  //   l
  //   Subtraction
  //   010
  //   l
  //   011
  //   l
  //   Divide
  //   100
  //   l
  //   101
  //   AND
  //   l
  //   OR
  //   110
  //   l
  //   HIGH
  //   111
  //   l
  //   ALU
  //   ALU Operation
  //   Multiplication
  //   -Ve num
  //   BCD
  //   SevenSegment Dec
endmodule
